// Logisim project СКНФ и МДНФ. Султанов.circ as structural Verilog
module \МДНФ  (
);

  wire and_1_out, and_2_out, and_3_out, and_4_out, and_5_out, and_6_out, and_7_out, and_8_out, and_9_out,
       and_10_out, or_1_out, or_2_out, or_3_out, or_4_out, x0_out, x1_out, x2_out, x3_out;

  Clock #(.highDuration(8), .lowDuration(8)) x3 (.out(x3_out));
  Clock #(.highDuration(4), .lowDuration(4)) x2 (.out(x2_out));
  Clock #(.highDuration(2), .lowDuration(2)) x1 (.out(x1_out));
  Clock x0 (.out(x0_out));
  main main_1 ();
  and and_1 (and_1_out, x3_out, ~x0_out);  // AND_Gate
  and and_2 (and_2_out, x2_out, x1_out);
  and and_3 (and_3_out, x3_out, x2_out);
  and and_4 (and_4_out, ~x2_out, ~x1_out);  // AND_Gate
  and and_5 (and_5_out, ~x3_out, ~x2_out);  // AND_Gate
  and and_6 (and_6_out, and_2_out, ~x0_out);  // AND_Gate
  and and_7 (and_7_out, and_3_out, x1_out);
  and and_8 (and_8_out, and_4_out, ~x0_out);  // AND_Gate
  and and_9 (and_9_out, and_5_out, x1_out);
  and and_10 (and_10_out, and_9_out, x0_out);
  or or_1 (or_1_out, and_1_out, and_6_out);
  or or_2 (or_2_out, or_1_out, and_7_out);
  or or_3 (or_3_out, or_2_out, and_8_out);
  or or_4 (or_4_out, or_3_out, and_10_out);
  LED led_1 (.in(or_4_out));
endmodule

module \СКНФ  (
);

  wire and_1_out, and_2_out, and_3_out, and_4_out, and_5_out, and_6_out, and_7_out, or_1_out, or_2_out,
       or_3_out, or_4_out, or_5_out, or_6_out, or_7_out, or_8_out, or_9_out, or_10_out, or_11_out, or_12_out,
       or_13_out, or_14_out, or_15_out, or_16_out, or_17_out, or_18_out, or_19_out, or_20_out, or_21_out,
       or_22_out, or_23_out, or_24_out, x0_out, x1_out, x2_out, x3_out;

  Clock #(.highDuration(8), .lowDuration(8)) x3 (.out(x3_out));
  Clock #(.highDuration(4), .lowDuration(4)) x2 (.out(x2_out));
  Clock #(.highDuration(2), .lowDuration(2)) x1 (.out(x1_out));
  Clock x0 (.out(x0_out));
  main main_1 ();
  or or_1 (or_1_out, x3_out, x2_out);
  or or_2 (or_2_out, or_1_out, x1_out);
  or or_3 (or_3_out, x3_out, x2_out);
  or or_4 (or_4_out, or_3_out, ~x1_out);  // OR_Gate
  or or_5 (or_5_out, x3_out, ~x2_out);  // OR_Gate
  or or_6 (or_6_out, or_5_out, x1_out);
  or or_7 (or_7_out, x3_out, ~x2_out);  // OR_Gate
  or or_8 (or_8_out, or_7_out, x1_out);
  or or_9 (or_9_out, x3_out, ~x2_out);  // OR_Gate
  or or_10 (or_10_out, or_9_out, ~x1_out);  // OR_Gate
  or or_11 (or_11_out, ~x3_out, x2_out);  // OR_Gate
  or or_12 (or_12_out, or_11_out, x1_out);
  or or_13 (or_13_out, ~x3_out, x2_out);  // OR_Gate
  or or_14 (or_14_out, or_13_out, ~x1_out);  // OR_Gate
  or or_15 (or_15_out, ~x3_out, ~x2_out);  // OR_Gate
  or or_16 (or_16_out, or_15_out, x1_out);
  or or_17 (or_17_out, or_2_out, ~x0_out);  // OR_Gate
  or or_18 (or_18_out, or_4_out, x0_out);
  or or_19 (or_19_out, or_6_out, x0_out);
  or or_20 (or_20_out, or_8_out, ~x0_out);  // OR_Gate
  or or_21 (or_21_out, or_10_out, ~x0_out);  // OR_Gate
  or or_22 (or_22_out, or_12_out, ~x0_out);  // OR_Gate
  or or_23 (or_23_out, or_14_out, ~x0_out);  // OR_Gate
  or or_24 (or_24_out, or_16_out, ~x0_out);  // OR_Gate
  and and_1 (and_1_out, or_17_out, or_18_out);
  and and_2 (and_2_out, and_1_out, or_19_out);
  and and_3 (and_3_out, and_2_out, or_20_out);
  and and_4 (and_4_out, and_3_out, or_21_out);
  and and_5 (and_5_out, and_4_out, or_22_out);
  and and_6 (and_6_out, and_5_out, or_23_out);
  and and_7 (and_7_out, and_6_out, or_24_out);
  LED led_1 (.in(and_7_out));
endmodule
