// Logisim project Finaly_square_root.circ as structural Verilog
module square_root (
  input  x7,
  input  x6,
  input  x5,
  input  x4,
  input  x3,
  input  x2,
  input  x1,
  input  x0
);

  wire a1_1_answer, a2_1_answer, a3_1_answer, a4_1_answer, a5_1_answer, a6_1_answer, a7_1_answer,
       a8_1_answer, a9_1_answer, a10_1_answer, a11_1_answer, a12_1_answer, a13_1_answer, a14_1_answer,
       a15_1_answer;
  wire [3:0] or_4_out;

  a0 a0_1 (.x7(x7), .x6(x6), .x5(x5), .x4(x4), .x3(x3), .x2(x2), .x1(x1), .x0(x0));  // open: answer
  a1 a1_1 (.x7(x7), .x6(x6), .x5(x5), .x4(x4), .x3(x3), .x2(x2), .x1(x1), .x0(x0), .answer(a1_1_answer));
  a2 a2_1 (.x7(x7), .x6(x6), .x5(x5), .x4(x4), .x3(x3), .x2(x2), .x1(x1), .x0(x0), .answer(a2_1_answer));
  a3 a3_1 (.x7(x7), .x6(x6), .x5(x5), .x4(x4), .x3(x3), .x2(x2), .x1(x1), .x0(x0), .answer(a3_1_answer));
  a4 a4_1 (.x7(x7), .x6(x6), .x5(x5), .x4(x4), .x3(x3), .x2(x2), .x1(x1), .x0(x0), .answer(a4_1_answer));
  a5 a5_1 (.x7(x7), .x6(x6), .x5(x5), .x4(x4), .x3(x3), .x2(x2), .x1(x1), .x0(x0), .answer(a5_1_answer));
  a6 a6_1 (.x7(x7), .x6(x6), .x5(x5), .x4(x4), .x3(x3), .x2(x2), .x1(x1), .x0(x0), .answer(a6_1_answer));
  a7 a7_1 (.x7(x7), .x6(x6), .x5(x5), .x4(x4), .x3(x3), .x2(x2), .x1(x1), .x0(x0), .answer(a7_1_answer));
  a8 a8_1 (.x7(x7), .x6(x6), .x5(x5), .x4(x4), .x3(x3), .x2(x2), .x1(x1), .x0(x0), .answer(a8_1_answer));
  a9 a9_1 (.x7(x7), .x6(x6), .x5(x5), .x4(x4), .x3(x3), .x2(x2), .x1(x1), .x0(x0), .answer(a9_1_answer));
  a10 a10_1 (.x7(x7), .x6(x6), .x5(x5), .x4(x4), .x3(x3), .x2(x2), .x1(x1), .x0(x0), .answer(a10_1_answer));
  a11 a11_1 (.x7(x7), .x6(x6), .x5(x5), .x4(x4), .x3(x3), .x2(x2), .x1(x1), .x0(x0), .answer(a11_1_answer));
  a12 a12_1 (.x7(x7), .x6(x6), .x5(x5), .x4(x4), .x3(x3), .x2(x2), .x1(x1), .x0(x0), .answer(a12_1_answer));
  a13 a13_1 (.x7(x7), .x6(x6), .x5(x5), .x4(x4), .x3(x3), .x2(x2), .x1(x1), .x0(x0), .answer(a13_1_answer));
  a14 a14_1 (.x7(x7), .x6(x6), .x5(x5), .x4(x4), .x3(x3), .x2(x2), .x1(x1), .x0(x0), .answer(a14_1_answer));
  a15 a15_1 (.x7(x7), .x6(x6), .x5(x5), .x4(x4), .x3(x3), .x2(x2), .x1(x1), .x0(x0), .answer(a15_1_answer));
  or or_1 (or_4_out[3], a15_1_answer, a14_1_answer, a13_1_answer, a12_1_answer, a11_1_answer, a10_1_answer, a9_1_answer, a8_1_answer);
  or or_2 (or_4_out[2], a15_1_answer, a14_1_answer, a13_1_answer, a12_1_answer, a7_1_answer, a6_1_answer, a5_1_answer, a4_1_answer);
  or or_3 (or_4_out[1], a2_1_answer, a3_1_answer, a6_1_answer, a7_1_answer, a10_1_answer, a11_1_answer, a14_1_answer, a15_1_answer);
  or or_4 (or_4_out[0], a1_1_answer, a3_1_answer, a5_1_answer, a7_1_answer, a9_1_answer, a11_1_answer, a13_1_answer, a15_1_answer);
  Hex_Digit_Display hex_digit_display_1 (.value(or_4_out));  // open: dp
endmodule

module a0 (
  input  x7,
  input  x6,
  input  x5,
  input  x4,
  input  x3,
  input  x2,
  input  x1,
  input  x0,
  output answer
);

  wire not_1_out, not_2_out, not_3_out, not_4_out, not_5_out, not_6_out, not_7_out, not_8_out;

  not not_1 (not_1_out, x7);
  not not_2 (not_2_out, x6);
  not not_3 (not_3_out, x5);
  not not_4 (not_4_out, x4);
  not not_5 (not_5_out, x3);
  not not_6 (not_6_out, x2);
  not not_7 (not_7_out, x1);
  not not_8 (not_8_out, x0);
  and and_1 (answer, not_1_out, not_2_out, not_3_out, not_4_out, not_5_out, not_6_out, not_7_out, not_8_out);
endmodule

module a1 (
  input  x7,
  input  x6,
  input  x5,
  input  x4,
  input  x3,
  input  x2,
  input  x1,
  input  x0,
  output answer
);

  wire and_1_out, and_2_out, not_1_out, not_2_out, not_3_out, not_4_out, not_5_out, not_6_out;

  not not_1 (not_1_out, x7);
  not not_2 (not_2_out, x6);
  not not_3 (not_3_out, x5);
  not not_4 (not_4_out, x4);
  not not_5 (not_5_out, x3);
  not not_6 (not_6_out, x2);
  and and_1 (and_1_out, not_1_out, not_2_out, not_3_out, not_4_out, not_5_out, not_6_out, x0);
  and and_2 (and_2_out, not_1_out, not_2_out, not_3_out, not_4_out, not_5_out, not_6_out, x1);
  or or_1 (answer, and_1_out, and_2_out);
endmodule

module a2 (
  input  x7,
  input  x6,
  input  x5,
  input  x4,
  input  x3,
  input  x2,
  input  x1,
  input  x0,
  output answer
);

  wire and_1_out, and_2_out, not_1_out, not_2_out, not_3_out, not_4_out, not_5_out, not_6_out, not_7_out,
       not_8_out;

  not not_1 (not_1_out, x7);
  not not_2 (not_2_out, x6);
  not not_3 (not_3_out, x5);
  not not_4 (not_4_out, x4);
  not not_5 (not_5_out, x3);
  not not_6 (not_6_out, x2);
  not not_7 (not_7_out, x1);
  not not_8 (not_8_out, x0);
  and and_1 (and_1_out, not_1_out, not_2_out, not_3_out, not_4_out, not_5_out, x2);
  and and_2 (and_2_out, not_1_out, not_2_out, not_3_out, not_4_out, x3, not_6_out, not_7_out, not_8_out);
  or or_1 (answer, and_1_out, and_2_out);
endmodule

module a3 (
  input  x7,
  input  x6,
  input  x5,
  input  x4,
  input  x3,
  input  x2,
  input  x1,
  input  x0,
  output answer
);

  wire and_1_out, and_2_out, and_3_out, not_1_out, not_2_out, not_3_out, not_4_out;

  not not_1 (not_1_out, x7);
  not not_2 (not_2_out, x6);
  not not_3 (not_3_out, x5);
  not not_4 (not_4_out, x4);
  and and_1 (and_1_out, not_1_out, not_2_out, not_3_out, not_4_out, x3, x0);
  and and_2 (and_2_out, not_1_out, not_2_out, not_3_out, not_4_out, x3, x1);
  and and_3 (and_3_out, not_1_out, not_2_out, not_3_out, not_4_out, x3, x2);
  or or_1 (answer, and_1_out, and_2_out, and_3_out);
endmodule

module a4 (
  input  x7,
  input  x6,
  input  x5,
  input  x4,
  input  x3,
  input  x2,
  input  x1,
  input  x0,
  output answer
);

  wire and_1_out, and_2_out, not_1_out, not_2_out, not_3_out, not_4_out, not_5_out, not_6_out, not_7_out;

  not not_1 (not_1_out, x7);
  not not_2 (not_2_out, x6);
  not not_3 (not_3_out, x5);
  not not_4 (not_4_out, x3);
  not not_5 (not_5_out, x2);
  not not_6 (not_6_out, x1);
  not not_7 (not_7_out, x0);
  and and_1 (and_1_out, not_1_out, not_2_out, not_3_out, x4, not_4_out);
  and and_2 (and_2_out, not_1_out, not_2_out, not_3_out, x4, not_5_out, not_6_out, not_7_out);
  or or_1 (answer, and_1_out, and_2_out);
endmodule

module a5 (
  input  x7,
  input  x6,
  input  x5,
  input  x4,
  input  x3,
  input  x2,
  input  x1,
  input  x0,
  output answer
);

  wire and_1_out, and_2_out, and_3_out, and_4_out, not_1_out, not_2_out, not_3_out, not_4_out, not_5_out,
       not_6_out;

  not not_1 (not_1_out, x7);
  not not_2 (not_2_out, x6);
  not not_3 (not_3_out, x5);
  not not_4 (not_4_out, x4);
  not not_5 (not_5_out, x3);
  not not_6 (not_6_out, x2);
  and and_1 (and_1_out, not_1_out, not_2_out, not_3_out, x4, x3, x0);
  and and_2 (and_2_out, not_1_out, not_2_out, not_3_out, x4, x3, x1);
  and and_3 (and_3_out, not_1_out, not_2_out, not_3_out, x4, x3, x2);
  and and_4 (and_4_out, not_1_out, not_2_out, x5, not_4_out, not_5_out, not_6_out);
  or or_1 (answer, and_1_out, and_2_out, and_3_out, and_4_out);
endmodule

module a6 (
  input  x7,
  input  x6,
  input  x5,
  input  x4,
  input  x3,
  input  x2,
  input  x1,
  input  x0,
  output answer
);

  wire and_1_out, and_2_out, and_3_out, not_1_out, not_2_out, not_3_out, not_4_out, not_5_out, not_6_out,
       not_7_out;

  not not_1 (not_1_out, x7);
  not not_2 (not_2_out, x6);
  not not_3 (not_3_out, x4);
  not not_4 (not_4_out, x3);
  not not_5 (not_5_out, x2);
  not not_6 (not_6_out, x1);
  not not_7 (not_7_out, x0);
  and and_1 (and_1_out, not_1_out, not_2_out, x5, not_3_out, x2);
  and and_2 (and_2_out, not_1_out, not_2_out, x5, not_3_out, x3);
  and and_3 (and_3_out, not_1_out, not_2_out, x5, x4, not_4_out, not_5_out, not_6_out, not_7_out);
  or or_1 (answer, and_1_out, and_2_out, and_3_out);
endmodule

module a7 (
  input  x7,
  input  x6,
  input  x5,
  input  x4,
  input  x3,
  input  x2,
  input  x1,
  input  x0,
  output answer
);

  wire and_1_out, and_2_out, and_3_out, and_4_out, not_1_out, not_2_out;

  not not_1 (not_1_out, x7);
  not not_2 (not_2_out, x6);
  and and_1 (and_1_out, not_1_out, not_2_out, x5, x4, x0);
  and and_2 (and_2_out, not_1_out, not_2_out, x5, x4, x1);
  and and_3 (and_3_out, not_1_out, not_2_out, x5, x4, x2);
  and and_4 (and_4_out, not_1_out, not_2_out, x5, x4, x3);
  or or_1 (answer, and_1_out, and_2_out, and_3_out, and_4_out);
endmodule

module a8 (
  input  x7,
  input  x6,
  input  x5,
  input  x4,
  input  x3,
  input  x2,
  input  x1,
  input  x0,
  output answer
);

  wire and_1_out, and_2_out, not_1_out, not_2_out, not_3_out, not_4_out, not_5_out, not_6_out, not_7_out;

  not not_1 (not_1_out, x7);
  not not_2 (not_2_out, x5);
  not not_3 (not_3_out, x4);
  not not_4 (not_4_out, x3);
  not not_5 (not_5_out, x2);
  not not_6 (not_6_out, x1);
  not not_7 (not_7_out, x0);
  and and_1 (and_1_out, not_1_out, x6, not_2_out, not_3_out);
  and and_2 (and_2_out, not_1_out, x6, not_2_out, not_4_out, not_5_out, not_6_out, not_7_out);
  or or_1 (answer, and_1_out, and_2_out);
endmodule

module a9 (
  input  x7,
  input  x6,
  input  x5,
  input  x4,
  input  x3,
  input  x2,
  input  x1,
  input  x0,
  output answer
);

  wire and_1_out, and_2_out, and_3_out, and_4_out, and_5_out, not_1_out, not_2_out, not_3_out, not_4_out,
       not_5_out;

  not not_1 (not_1_out, x7);
  not not_2 (not_2_out, x5);
  not not_3 (not_3_out, x4);
  not not_4 (not_4_out, x3);
  not not_5 (not_5_out, x2);
  and and_1 (and_1_out, not_1_out, x6, not_2_out, x4, x0);
  and and_2 (and_2_out, not_1_out, x6, not_2_out, x4, x1);
  and and_3 (and_3_out, not_1_out, x6, not_2_out, x4, x2);
  and and_4 (and_4_out, not_1_out, x6, not_2_out, x4, x3);
  and and_5 (and_5_out, not_1_out, x6, x5, not_3_out, not_4_out, not_5_out);
  or or_1 (answer, and_1_out, and_2_out, and_3_out, and_4_out, and_5_out);
endmodule

module a10 (
  input  x7,
  input  x6,
  input  x5,
  input  x4,
  input  x3,
  input  x2,
  input  x1,
  input  x0,
  output answer
);

  wire and_1_out, and_2_out, and_3_out, and_4_out, not_1_out, not_2_out, not_3_out, not_4_out, not_5_out,
       not_6_out;

  not not_1 (not_1_out, x7);
  not not_2 (not_2_out, x4);
  not not_3 (not_3_out, x3);
  not not_4 (not_4_out, x2);
  not not_5 (not_5_out, x1);
  not not_6 (not_6_out, x0);
  and and_1 (and_1_out, not_1_out, x6, x5, not_3_out, x2);
  and and_2 (and_2_out, not_1_out, x6, x5, not_2_out, x3);
  and and_3 (and_3_out, not_1_out, x6, x5, x4, not_3_out);
  and and_4 (and_4_out, not_1_out, x6, x5, x4, not_4_out, not_5_out, not_6_out);
  or or_1 (answer, and_1_out, and_2_out, and_3_out, and_4_out);
endmodule

module a11 (
  input  x7,
  input  x6,
  input  x5,
  input  x4,
  input  x3,
  input  x2,
  input  x1,
  input  x0,
  output answer
);

  wire and_1_out, and_2_out, and_3_out, and_4_out, not_1_out, not_2_out, not_3_out, not_4_out;

  not not_1 (not_1_out, x7);
  not not_2 (not_2_out, x6);
  not not_3 (not_3_out, x5);
  not not_4 (not_4_out, x4);
  and and_1 (and_1_out, not_1_out, x6, x5, x4, x3, x0);
  and and_2 (and_2_out, not_1_out, x6, x5, x4, x3, x1);
  and and_3 (and_3_out, not_1_out, x6, x5, x4, x3, x2);
  and and_4 (and_4_out, x7, not_2_out, not_3_out, not_4_out);
  or or_1 (answer, and_1_out, and_2_out, and_3_out, and_4_out);
endmodule

module a12 (
  input  x7,
  input  x6,
  input  x5,
  input  x4,
  input  x3,
  input  x2,
  input  x1,
  input  x0,
  output answer
);

  wire and_1_out, and_2_out, and_3_out, not_1_out, not_2_out, not_3_out, not_4_out, not_5_out, not_6_out,
       not_7_out;

  not not_1 (not_1_out, x6);
  not not_2 (not_2_out, x5);
  not not_3 (not_3_out, x4);
  not not_4 (not_4_out, x3);
  not not_5 (not_5_out, x2);
  not not_6 (not_6_out, x1);
  not not_7 (not_7_out, x0);
  and and_1 (and_1_out, x7, not_1_out, not_2_out, x4);
  and and_2 (and_2_out, x7, not_1_out, x5, not_3_out, not_4_out);
  and and_3 (and_3_out, x7, not_1_out, x5, not_3_out, not_5_out, not_6_out, not_7_out);
  or or_1 (answer, and_1_out, and_2_out, and_3_out);
endmodule

module a13 (
  input  x7,
  input  x6,
  input  x5,
  input  x4,
  input  x3,
  input  x2,
  input  x1,
  input  x0,
  output answer
);

  wire and_1_out, and_2_out, and_3_out, and_4_out, and_5_out, not_1_out, not_2_out, not_3_out, not_4_out,
       not_5_out;

  not not_1 (not_1_out, x6);
  not not_2 (not_2_out, x5);
  not not_3 (not_3_out, x4);
  not not_4 (not_4_out, x3);
  not not_5 (not_5_out, x2);
  and and_1 (and_1_out, x7, not_1_out, x5, x3, x0);
  and and_2 (and_2_out, x7, not_1_out, x5, x3, x1);
  and and_3 (and_3_out, x7, not_1_out, x5, x3, x2);
  and and_4 (and_4_out, x7, not_1_out, x5, x4);
  and and_5 (and_5_out, x7, x6, not_2_out, not_3_out, not_4_out, not_5_out);
  or or_1 (answer, and_1_out, and_2_out, and_3_out, and_4_out, and_5_out);
endmodule

module a14 (
  input  x7,
  input  x6,
  input  x5,
  input  x4,
  input  x3,
  input  x2,
  input  x1,
  input  x0,
  output answer
);

  wire and_1_out, and_2_out, and_3_out, and_4_out, not_1_out, not_2_out, not_3_out, not_4_out, not_5_out,
       not_6_out;

  not not_1 (not_1_out, x5);
  not not_2 (not_2_out, x4);
  not not_3 (not_3_out, x3);
  not not_4 (not_4_out, x2);
  not not_5 (not_5_out, x1);
  not not_6 (not_6_out, x0);
  and and_1 (and_1_out, x7, x6, not_1_out, x2);
  and and_2 (and_2_out, x7, x6, not_1_out, x3);
  and and_3 (and_3_out, x7, x6, not_1_out, x4);
  and and_4 (and_4_out, x7, x6, x5, not_2_out, not_3_out, not_4_out, not_5_out, not_6_out);
  or or_1 (answer, and_1_out, and_2_out, and_3_out, and_4_out);
endmodule

module a15 (
  input  x7,
  input  x6,
  input  x5,
  input  x4,
  input  x3,
  input  x2,
  input  x1,
  input  x0,
  output answer
);

  wire and_1_out, and_2_out, and_3_out, and_4_out, and_5_out;

  and and_1 (and_1_out, x7, x6, x5, x0);
  and and_2 (and_2_out, x7, x6, x5, x1);
  and and_3 (and_3_out, x7, x6, x5, x2);
  and and_4 (and_4_out, x7, x6, x5, x3);
  and and_5 (and_5_out, x7, x6, x5, x4);
  or or_1 (answer, and_1_out, and_2_out, and_3_out, and_4_out, and_5_out);
endmodule
