// Logisim project JK trigger on RS.circ as structural Verilog: 1 circuit, main circuit main
module main (
);

  wire and_1_out, and_2_out, C_out, J_out, K_out, not_1_out, s_r_ff_1_q, s_r_ff_1_qn, s_r_ff_2_q, s_r_ff_2_qn;

  Clock J (.out(J_out));
  Clock #(.highDuration(2), .lowDuration(2)) C (.out(C_out));
  Clock #(.highDuration(4), .lowDuration(4)) K (.out(K_out));
  and and_1 (and_1_out, s_r_ff_2_qn, J_out);
  and and_2 (and_2_out, K_out, s_r_ff_2_q);
  S_R_Flip_Flop s_r_ff_1 (
    .S(and_1_out), .clk(C_out), .R(and_2_out), .Q(s_r_ff_1_q), .Qn(s_r_ff_1_qn));  // open: preset, reset, en
  not not_1 (not_1_out, C_out);
  S_R_Flip_Flop s_r_ff_2 (
    .S(s_r_ff_1_q), .clk(not_1_out), .R(s_r_ff_1_qn), .Q(s_r_ff_2_q), .Qn(s_r_ff_2_qn));  // open: preset, reset, en
endmodule
