// Logisim project T trigger on RS.circ as structural Verilog: 1 circuit, main circuit main
module main (
);

  wire and_1_out, and_2_out, C_out, not_1_out, not_2_out, s_r_ff_1_q, s_r_ff_1_qn, s_r_ff_2_q, s_r_ff_2_qn,
       T_out;

  Clock T (.out(T_out));
  and and_1 (and_1_out, s_r_ff_2_qn, T_out);
  Clock #(.highDuration(2), .lowDuration(2)) C (.out(C_out));
  not not_1 (not_1_out, C_out);
  and and_2 (and_2_out, T_out, s_r_ff_2_q);
  S_R_Flip_Flop s_r_ff_1 (
    .S(and_1_out), .clk(not_1_out), .R(and_2_out), .Q(s_r_ff_1_q), .Qn(s_r_ff_1_qn));  // open: preset, reset, en
  not not_2 (not_2_out, not_1_out);
  S_R_Flip_Flop s_r_ff_2 (
    .S(s_r_ff_1_q), .clk(not_2_out), .R(s_r_ff_1_qn), .Q(s_r_ff_2_q), .Qn(s_r_ff_2_qn));  // open: preset, reset, en
endmodule
