// Logisim project Синхронный счётчик с параллельным переносом по модулю 14.circ as structural Verilog: 1 circuit, main circuit main
module main (
  input  in_1
);

  wire and_1_out, and_2_out, and_3_out, and_4_out, C_out, or_1_out, or_2_out, t_ff_1_q, t_ff_2_q, t_ff_2_qn,
       t_ff_3_q, t_ff_4_q;

  Clock C (.out(C_out));
  and and_1 (and_1_out, t_ff_1_q, t_ff_2_q);
  and and_2 (and_2_out, t_ff_1_q, t_ff_2_q, t_ff_3_q);
  or or_1 (or_1_out, and_2_out, and_4_out);
  or or_2 (or_2_out, and_1_out, and_4_out);
  and and_3 (and_3_out, t_ff_1_q, ~and_4_out);  // AND_Gate
  T_Flip_Flop t_ff_1 (.clk(C_out), .T(in_1), .Q(t_ff_1_q));  // open: Qn, preset, reset, en
  T_Flip_Flop t_ff_2 (.clk(C_out), .T(and_3_out), .Q(t_ff_2_q), .Qn(t_ff_2_qn));  // open: preset, reset, en
  T_Flip_Flop t_ff_3 (.clk(C_out), .T(or_2_out), .Q(t_ff_3_q));  // open: Qn, preset, reset, en
  T_Flip_Flop t_ff_4 (.clk(C_out), .T(or_1_out), .Q(t_ff_4_q));  // open: Qn, preset, reset, en
  and and_4 (and_4_out, t_ff_1_q, t_ff_2_qn, t_ff_3_q, t_ff_4_q);
  LED led_1 (.in(t_ff_1_q));
  LED led_2 (.in(t_ff_2_q));
  LED led_3 (.in(t_ff_3_q));
  LED led_4 (.in(t_ff_4_q));
endmodule
