// Logisim project Синхронный счётчик с параллельным переносом по модулю 16.circ as structural Verilog: 1 circuit, main circuit main
module main (
  input  in_1
);

  wire and_1_out, and_2_out, C_out, t_ff_1_q, t_ff_2_q, t_ff_3_q, t_ff_4_q;

  Clock C (.out(C_out));
  and and_1 (and_1_out, t_ff_1_q, t_ff_2_q);
  and and_2 (and_2_out, t_ff_1_q, t_ff_2_q, t_ff_3_q);
  T_Flip_Flop t_ff_1 (.clk(C_out), .T(in_1), .Q(t_ff_1_q));  // open: Qn, preset, reset, en
  T_Flip_Flop t_ff_2 (.clk(C_out), .T(t_ff_1_q), .Q(t_ff_2_q));  // open: Qn, preset, reset, en
  T_Flip_Flop t_ff_3 (.clk(C_out), .T(and_1_out), .Q(t_ff_3_q));  // open: Qn, preset, reset, en
  T_Flip_Flop t_ff_4 (.clk(C_out), .T(and_2_out), .Q(t_ff_4_q));  // open: Qn, preset, reset, en
  LED _1 (.in(t_ff_1_q));
  LED _2 (.in(t_ff_2_q));
  LED _4 (.in(t_ff_3_q));
  LED _8 (.in(t_ff_4_q));
endmodule
