// Logisim project Синхронный счётчик с параллельным переносом по модулю 12.circ as structural Verilog
module RS_Trigger (
  input  S,
  input  C,
  input  R,
  output Q,
  output notQ
);

  wire nand_1_out, nand_2_out;

  nand nand_1 (nand_1_out, S, C);
  nand nand_2 (nand_2_out, C, R);
  nand nand_3 (Q, notQ, nand_1_out);
  nand nand_4 (notQ, nand_2_out, Q);
endmodule

module JK_Trigger_on_RS (
  input  reset,
  input  J,
  input  C,
  input  K,
  output Q,
  output notQ
);

  wire and_1_out, and_2_out, not_1_out, or_1_out, or_2_out, rs_trigger_2_notq, rs_trigger_2_q;

  and and_1 (and_1_out, rs_trigger_2_notq, J);
  and and_2 (and_2_out, K, rs_trigger_2_q);
  or or_1 (or_1_out, and_2_out, reset);
  or or_2 (or_2_out, reset, C);
  RS_Trigger rs_trigger_1 (.S(and_1_out), .C(or_2_out), .R(or_1_out), .Q(Q), .notQ(notQ));
  not not_1 (not_1_out, or_2_out);
  RS_Trigger rs_trigger_2 (.S(Q), .C(not_1_out), .R(notQ), .Q(rs_trigger_2_q), .notQ(rs_trigger_2_notq));
endmodule

module JK_Trigger (
  input  reset,
  input  J,
  input  C,
  input  K,
  output Q,
  output not_Q
);

  wire nand_1_out, nand_2_out, nand_3_out, nand_4_out, nand_5_out, nand_6_out, nand_7_out;

  nand nand_1 (nand_1_out, not_Q, J, C);
  nand nand_2 (nand_2_out, C, K, Q);
  nand nand_3 (nand_3_out, nand_1_out, nand_4_out);
  nand nand_4 (nand_4_out, nand_3_out, nand_2_out);
  nand nand_5 (nand_5_out, C, C);
  nand nand_6 (nand_6_out, nand_3_out, nand_5_out);
  nand nand_7 (nand_7_out, nand_5_out, nand_4_out);
  nand nand_8 (Q, nand_6_out, not_Q);
  nand nand_9 (not_Q, Q, nand_7_out);
endmodule

module T_Trigger_on_JK (
  input  reset,
  input  T,
  input  C,
  output Q,
  output notQ
);

  JK_Trigger_on_RS jk_trigger_on_rs_1 (.reset(reset), .J(T), .C(C), .K(T), .Q(Q), .notQ(notQ));
endmodule

module Counter_mod_16 (
  input  CE
);

  wire and_1_out, and_2_out, C_out, not_1_out, not_2_out, not_3_out, not_4_out, not_5_out, reset_out,
       rs_trigger_1_q, rs_trigger_2_q, rs_trigger_3_q;
  wire [3:0] t_trigger_on_jk_1_q;

  Button reset (.out(reset_out));
  Clock C (.out(C_out));
  not not_1 (not_1_out, C_out);
  not not_2 (not_2_out, t_trigger_on_jk_1_q[0]);
  and and_1 (and_1_out, t_trigger_on_jk_1_q[0], t_trigger_on_jk_1_q[1]);
  not not_3 (not_3_out, C_out);
  and and_2 (and_2_out, t_trigger_on_jk_1_q[2], t_trigger_on_jk_1_q[1], t_trigger_on_jk_1_q[0]);
  not not_4 (not_4_out, and_1_out);
  not not_5 (not_5_out, and_2_out);
  RS_Trigger rs_trigger_1 (.S(t_trigger_on_jk_1_q[0]), .C(not_1_out), .R(not_2_out), .Q(rs_trigger_1_q));  // open: notQ
  RS_Trigger rs_trigger_2 (.S(and_1_out), .C(not_3_out), .R(not_4_out), .Q(rs_trigger_2_q));  // open: notQ
  RS_Trigger rs_trigger_3 (.S(and_2_out), .C(not_3_out), .R(not_5_out), .Q(rs_trigger_3_q));  // open: notQ
  T_Trigger_on_JK t_trigger_on_jk_1 (.reset(reset_out), .T(CE), .C(C_out), .Q(t_trigger_on_jk_1_q[0]));  // open: notQ
  T_Trigger_on_JK t_trigger_on_jk_2 (
    .reset(reset_out), .T(rs_trigger_1_q), .C(C_out), .Q(t_trigger_on_jk_1_q[1]));  // open: notQ
  T_Trigger_on_JK t_trigger_on_jk_3 (
    .reset(reset_out), .T(rs_trigger_2_q), .C(C_out), .Q(t_trigger_on_jk_1_q[2]));  // open: notQ
  T_Trigger_on_JK t_trigger_on_jk_4 (
    .reset(reset_out), .T(rs_trigger_3_q), .C(C_out), .Q(t_trigger_on_jk_1_q[3]));  // open: notQ
  Hex_Digit_Display hex_digit_display_1 (.value(t_trigger_on_jk_1_q));  // open: dp
endmodule

module Counter_mod_12 (
  input  CE
);

  wire and_1_out, and_2_out, and_3_out, and_4_out, C_out, not_1_out, not_2_out, not_3_out, not_4_out,
       not_5_out, or_1_out, reset_out, rs_trigger_1_q, rs_trigger_2_q, rs_trigger_3_q;
  wire [3:0] t_trigger_on_jk_1_q;

  Button reset (.out(reset_out));
  Clock C (.out(C_out));
  not not_1 (not_1_out, C_out);
  not not_2 (not_2_out, t_trigger_on_jk_1_q[0]);
  and and_1 (and_1_out, t_trigger_on_jk_1_q[0], t_trigger_on_jk_1_q[1]);
  not not_3 (not_3_out, C_out);
  and and_2 (and_2_out, t_trigger_on_jk_1_q[2], t_trigger_on_jk_1_q[1], t_trigger_on_jk_1_q[0]);
  and and_3 (and_3_out, and_1_out, ~and_4_out);  // AND_Gate
  or or_1 (or_1_out, and_2_out, and_4_out);
  not not_4 (not_4_out, and_3_out);
  not not_5 (not_5_out, or_1_out);
  RS_Trigger rs_trigger_1 (.S(t_trigger_on_jk_1_q[0]), .C(not_1_out), .R(not_2_out), .Q(rs_trigger_1_q));  // open: notQ
  RS_Trigger rs_trigger_2 (.S(and_3_out), .C(not_3_out), .R(not_4_out), .Q(rs_trigger_2_q));  // open: notQ
  RS_Trigger rs_trigger_3 (.S(or_1_out), .C(not_3_out), .R(not_5_out), .Q(rs_trigger_3_q));  // open: notQ
  T_Trigger_on_JK t_trigger_on_jk_1 (.reset(reset_out), .T(CE), .C(C_out), .Q(t_trigger_on_jk_1_q[0]));  // open: notQ
  T_Trigger_on_JK t_trigger_on_jk_2 (
    .reset(reset_out), .T(rs_trigger_1_q), .C(C_out), .Q(t_trigger_on_jk_1_q[1]));  // open: notQ
  T_Trigger_on_JK t_trigger_on_jk_3 (
    .reset(reset_out), .T(rs_trigger_2_q), .C(C_out), .Q(t_trigger_on_jk_1_q[2]));  // open: notQ
  T_Trigger_on_JK t_trigger_on_jk_4 (
    .reset(reset_out), .T(rs_trigger_3_q), .C(C_out), .Q(t_trigger_on_jk_1_q[3]));  // open: notQ
  Hex_Digit_Display hex_digit_display_1 (.value(t_trigger_on_jk_1_q));  // open: dp
  and and_4 (and_4_out, t_trigger_on_jk_1_q[0], t_trigger_on_jk_1_q[1], ~t_trigger_on_jk_1_q[2], t_trigger_on_jk_1_q[3], ~C_out);  // AND_Gate
endmodule
