// Logisim project МКНФ.circ as structural Verilog: 1 circuit, main circuit main
module main (
);

  wire and_1_out, or_1_out, or_2_out, or_3_out, or_4_out, x0_out, x1_out, x2_out, x3_out;

  Clock #(.highDuration(8), .lowDuration(8)) x3 (.out(x3_out));
  Clock #(.highDuration(4), .lowDuration(4)) x2 (.out(x2_out));
  Clock #(.highDuration(2), .lowDuration(2)) x1 (.out(x1_out));
  Clock x0 (.out(x0_out));
  or or_1 (or_1_out, ~x3_out, ~x2_out, x1_out);  // OR_Gate
  or or_2 (or_2_out, ~x3_out, ~x1_out, x0_out);  // OR_Gate
  or or_3 (or_3_out, x3_out, x1_out, x0_out);
  or or_4 (or_4_out, x3_out, x2_out, ~x1_out);  // OR_Gate
  LED led_1 (.in(and_1_out));
  and and_1 (and_1_out, or_1_out, or_2_out, or_3_out, or_4_out);
endmodule
