// Logisim project СКНФ_____в первой версии СКНФ опечатка в третьем с конца дизъюнкте.circ as structural Verilog: 1 circuit, main circuit main
module main (
);

  wire and_1_out, or_1_out, or_2_out, or_3_out, or_4_out, or_5_out, or_6_out, or_7_out, or_8_out, x0_out,
       x1_out, x2_out, x3_out;

  Clock #(.highDuration(8), .lowDuration(8)) x3 (.out(x3_out));
  Clock #(.highDuration(4), .lowDuration(4)) x2 (.out(x2_out));
  Clock #(.highDuration(2), .lowDuration(2)) x1 (.out(x1_out));
  Clock x0 (.out(x0_out));
  or or_1 (or_1_out, x3_out, x2_out, x1_out, x0_out);
  or or_2 (or_2_out, x3_out, x2_out, ~x1_out, x0_out);  // OR_Gate
  or or_3 (or_3_out, x3_out, x2_out, ~x1_out, ~x0_out);  // OR_Gate
  or or_4 (or_4_out, x3_out, ~x2_out, x1_out, x0_out);  // OR_Gate
  or or_5 (or_5_out, ~x3_out, x2_out, ~x1_out, x0_out);  // OR_Gate
  or or_6 (or_6_out, ~x3_out, ~x2_out, x1_out, ~x0_out);  // OR_Gate
  or or_7 (or_7_out, ~x3_out, ~x2_out, x1_out, ~x0_out);  // OR_Gate
  or or_8 (or_8_out, ~x3_out, ~x2_out, ~x1_out, x0_out);  // OR_Gate
  and and_1 (and_1_out, or_1_out, or_2_out, or_3_out, or_4_out, or_5_out, or_6_out, or_7_out, or_8_out);
  LED led_1 (.in(and_1_out));
endmodule
