// Logisim project schetchik_na_T-triggerakh.circ as structural Verilog: 1 circuit, main circuit main
module main (
  input  in_1
);

  wire clock_1_out, t_ff_1_q, t_ff_2_q, t_ff_3_q, t_ff_4_q, t_ff_5_q, t_ff_6_q, t_ff_7_q, t_ff_8_q, t_ff_9_q,
       t_ff_10_q, t_ff_11_q, t_ff_12_q, t_ff_13_q;

  Clock clock_1 (.out(clock_1_out));
  LED led_1 (.in(t_ff_1_q));
  T_Flip_Flop t_ff_1 (.clk(clock_1_out), .T(in_1), .Q(t_ff_1_q));  // open: Qn, preset, reset, en
  LED led_2 (.in(t_ff_2_q));
  T_Flip_Flop t_ff_2 (.clk(t_ff_1_q), .T(in_1), .Q(t_ff_2_q));  // open: Qn, preset, reset, en
  LED led_3 (.in(t_ff_3_q));
  T_Flip_Flop t_ff_3 (.clk(t_ff_2_q), .T(in_1), .Q(t_ff_3_q));  // open: Qn, preset, reset, en
  T_Flip_Flop t_ff_4 (.clk(t_ff_3_q), .T(in_1), .Q(t_ff_4_q));  // open: Qn, preset, reset, en
  LED led_4 (.in(t_ff_5_q));
  LED led_5 (.in(t_ff_4_q));
  T_Flip_Flop t_ff_5 (.clk(t_ff_4_q), .T(in_1), .Q(t_ff_5_q));  // open: Qn, preset, reset, en
  LED led_6 (.in(t_ff_6_q));
  T_Flip_Flop t_ff_6 (.clk(t_ff_5_q), .T(in_1), .Q(t_ff_6_q));  // open: Qn, preset, reset, en
  LED led_7 (.in(t_ff_7_q));
  T_Flip_Flop t_ff_7 (.clk(t_ff_6_q), .T(in_1), .Q(t_ff_7_q));  // open: Qn, preset, reset, en
  LED led_8 (.in(t_ff_8_q));
  T_Flip_Flop t_ff_8 (.clk(t_ff_7_q), .T(in_1), .Q(t_ff_8_q));  // open: Qn, preset, reset, en
  LED led_9 (.in(t_ff_9_q));
  T_Flip_Flop t_ff_9 (.clk(t_ff_8_q), .T(in_1), .Q(t_ff_9_q));  // open: Qn, preset, reset, en
  LED led_10 (.in(t_ff_10_q));
  T_Flip_Flop t_ff_10 (.clk(t_ff_9_q), .T(in_1), .Q(t_ff_10_q));  // open: Qn, preset, reset, en
  LED led_11 (.in(t_ff_11_q));
  T_Flip_Flop t_ff_11 (.clk(t_ff_10_q), .T(in_1), .Q(t_ff_11_q));  // open: Qn, preset, reset, en
  T_Flip_Flop t_ff_12 (.clk(t_ff_11_q), .T(in_1), .Q(t_ff_12_q));  // open: Qn, preset, reset, en
  LED led_12 (.in(t_ff_13_q));
  LED led_13 (.in(t_ff_12_q));
  T_Flip_Flop t_ff_13 (.clk(t_ff_12_q), .T(in_1), .Q(t_ff_13_q));  // open: Qn, preset, reset, en
endmodule
